# Fritzing sketch sensor (saved by Fritzing 0.9.2b)
circuit board: 2.3cm x 3.05cm
breadboards: 1

parts:
  IC1 = IC, DIP package, 8 pins [chip_label=IC]
  RHT1 = Humidity and Temperature Sensor RHT03
  VCC1 = Battery
  J1 = shrouded pin header, 8 pins [form="♂ (shrouded male)"]
  R1 = Resistor [tolerance=±5% resistance=1k package=THT]
  LED1 = LED - 5mm [color="Red (633nm)" package="5 mm [THT]"]
  J2 = female pin header, 2 pins [form="♀ (female)"]

nets:
  N1: IC1.pin2, J1.pin1
  N2: IC1.pin3, RHT1.Data-signal
  N3: IC1.pin4, RHT1.GND_2, VCC1.-, J1.pin5, R1.Pin_1
  N4: IC1.pin5, J1.pin7
  N5: IC1.pin6, J1.pin6, J2.pin2
  N6: IC1.pin7, J1.pin3, J2.pin1
  N7: IC1.pin8, RHT1.Vcc, VCC1.+, J1.pin4
  N8: J1.pin8, LED1.anode
  N9: R1.Pin_0, LED1.cathode
